# Fritzing sketch Fritzing Sketch (saved by Fritzing 0.9.3b)

parts:
  Part1 = Matrix LED de 8x8 basada en MAX7219
  TM1638_Led_and_Key1 = TM1638_Led_and_Key [package=THT]
  Part2 = Arduino Nano (Rev3.0)

nets:
  VCC: Part1.VCC, TM1638_Led_and_Key1.VCC, Part2.5V
  GND: Part1.GND, TM1638_Led_and_Key1.GND, Part2.GND
  N1: Part1.CS, Part2.D4
  N2: Part1.CLK, Part2.D5
  N3: Part1.DIN, Part2.D3
  N4: TM1638_Led_and_Key1.STB, Part2.D7
  N5: TM1638_Led_and_Key1.CLK, Part2.D8
  N6: TM1638_Led_and_Key1.DIO, Part2.D9
